# Fritzing sketch typing-challenge (saved by Fritzing 0.9.6b)
breadboards: 1

parts:
  Part1 = Arduino Uno (Rev3)
  X1 = USB Connectors [package=usb-microb]
  LCD1 = LCD screen
  R1 = Rotary Potentiometer (Small) [maximum_resistance=0.1MΩ package=THT]

nets:
  N1: Part1.D10_PWM/SS, LCD1.DB4
  N2: Part1.D11_PWM/MOSI, LCD1.DB5
  N3: Part1.D12/MISO, LCD1.DB6
  N4: Part1.D13/SCK, LCD1.DB7
  GND: Part1.GND, X1.GND, LCD1.VSS, LCD1.R/W, LCD1.LED-, R1.leg2
  N5: Part1.D2, X1.VBUS
  N6: Part1.D3_PWM, X1.D-
  N7: Part1.D4, LCD1.RS
  N8: Part1.D6_PWM, LCD1.E
  N9: Part1.3V3, LCD1.LED+
  5V: Part1.5V, X1.D+, LCD1.VDD, R1.leg1
  N10: LCD1.V0, R1.wiper
